// Logisim project hack.circ as structural Verilog: 4 circuits, main circuit ALU
module ALU (
  input  [15:0] x,
  input  zx,
  input  nx,
  input  [15:0] y,
  input  zy,
  input  ny,
  input  f,
  input  no,
  output [15:0] out,
  output zr,
  output ng
);

  wire [15:0] adder_1_out, and_1_out, multiplexer_1_out, multiplexer_2_out, multiplexer_3_out,
       multiplexer_4_out, multiplexer_5_out, not_1_out, not_2_out, not_3_out;

  Multiplexer #(.width(16), .enable("false")) multiplexer_1 (
    .in0(x), .in1({16{1'b0}}), .out(multiplexer_1_out), .sel(zx));
  Multiplexer #(.width(16), .enable("false")) multiplexer_2 (
    .in0(y), .in1({16{1'b0}}), .out(multiplexer_2_out), .sel(zy));
  assign not_1_out = ~multiplexer_1_out;  // NOT_Gate not_1, 16 bits wide
  assign not_2_out = ~multiplexer_2_out;  // NOT_Gate not_2, 16 bits wide
  Multiplexer #(.width(16), .enable("false")) multiplexer_3 (
    .in0(multiplexer_1_out), .in1(not_1_out), .out(multiplexer_3_out), .sel(nx));
  Multiplexer #(.width(16), .enable("false")) multiplexer_4 (
    .in0(multiplexer_2_out), .in1(not_2_out), .out(multiplexer_4_out), .sel(ny));
  assign and_1_out = multiplexer_3_out & multiplexer_4_out;  // AND_Gate and_1, 16 bits wide
  Adder #(.width(16)) adder_1 (.a(multiplexer_3_out), .b(multiplexer_4_out), .out(adder_1_out));  // open: cin, cout
  Multiplexer #(.width(16), .enable("false")) multiplexer_5 (
    .in0(and_1_out), .in1(adder_1_out), .out(multiplexer_5_out), .sel(f));
  assign not_3_out = ~multiplexer_5_out;  // NOT_Gate not_3, 16 bits wide
  Multiplexer #(.width(16), .enable("false")) multiplexer_6 (
    .in0(multiplexer_5_out), .in1(not_3_out), .out({ng, out[14:0]}), .sel(no));
  nor nor_1 (zr, out[0], out[1], out[2], out[3], out[4], out[5], out[6], out[7], out[8], out[9], out[10], out[11], out[12], out[13], out[14], ng);

  assign out[15] = ng;
endmodule

module PC (
  input  reset,
  input  load,
  input  inc,
  input  clk,
  input  [15:0] in,
  output [15:0] out
);

  wire or_1_out;
  wire [15:0] adder_1_out, multiplexer_1_out;

  or or_1 (or_1_out, reset, load, inc);
  Adder #(.width(16)) adder_1 (.a(out), .b(16'h1), .out(adder_1_out), .cin(1'b0));  // open: cout
  Register #(.width(16)) register_1 (.D(multiplexer_1_out), .en(or_1_out), .Q(out), .clk(clk), .clr(1'b0));
  Multiplexer #(.select(3), .width(16), .enable("false")) multiplexer_1 (
    .in0({16{1'b0}}), .in1(adder_1_out), .in2(in), .in3(in), .in4({16{1'b0}}), .in5({16{1'b0}}),
    .in6({16{1'b0}}), .in7({16{1'b0}}), .out(multiplexer_1_out), .sel({reset, load, inc}));
endmodule

module CPU (
  input  clk,
  input  [15:0] Instruction,
  input  [15:0] inM,
  input  Reset,
  input  in_5,
  output [15:0] outM,
  output writeM,
  output [14:0] addressM,
  output [14:0] pc
);

  wire and_1_out, and_2_out, and_3_out, loadA, loadD, loadPC, ng, or_1_out, or_2_out, selA, zr;
  wire [15:0] D_q, multiplexer_1_out, multiplexer_2_out;
  wire [15:15] A_q, pc_1_out;

  or or_1 (or_1_out, zr, ng);
  and and_1 (and_1_out, Instruction[0], or_1_out);
  and and_2 (and_2_out, Instruction[1], zr);
  and and_3 (and_3_out, Instruction[2], ng);
  Multiplexer #(.width(16), .enable("false")) multiplexer_1 (
    .in0(outM), .in1(Instruction), .out(multiplexer_1_out), .sel(selA));
  Register #(.width(16)) A (.D(multiplexer_1_out), .en(loadA), .Q({A_q[15], addressM}), .clk(clk));  // open: clr
  or or_2 (or_2_out, and_1_out, and_2_out, and_3_out);
  Register #(.width(16)) D (.D(outM), .en(loadD), .Q(D_q), .clk(clk));  // open: clr
  Multiplexer #(.width(16), .enable("false")) multiplexer_2 (
    .in0({A_q[15], addressM}), .in1(inM), .out(multiplexer_2_out), .sel(Instruction[12]));
  and and_4 (loadPC, or_2_out, Instruction[15]);
  ALU alu_1 (
    .x(D_q), .y(multiplexer_2_out), .zx(Instruction[11]), .nx(Instruction[10]), .zy(Instruction[9]),
    .ny(Instruction[8]), .f(Instruction[7]), .no(Instruction[6]), .out(outM), .ng(ng), .zr(zr));
  PC pc_1 (.reset(Reset), .load(loadPC), .inc(1'b1), .clk(clk), .in({A_q[15], addressM}), .out({pc_1_out[15], pc}));
  and and_5 (selA, Instruction[5], Instruction[15]);
  or or_3 (loadA, Instruction[5], ~Instruction[15]);  // OR_Gate
  and and_6 (loadD, Instruction[4], Instruction[15]);
  and and_7 (writeM, Instruction[3], Instruction[15]);

  // Other names for the same wires on the sheet: i0 = Instruction[0]; i1 = Instruction[1]; i2 = Instruction[2];
  //   i3 = Instruction[3]; i4 = Instruction[4]; i5 = Instruction[5]; no = Instruction[6]; f = Instruction[7];
  //   ny = Instruction[8]; zy = Instruction[9]; nx = Instruction[10]; zx = Instruction[11]; AorM = Instruction[12];
  //   i12 = Instruction[12]; i13 = Instruction[13]; i14 = Instruction[14]; i15 = Instruction[15]
endmodule

module CU (
  input  [15:0] instruction,
  input  zr,
  input  ng,
  output selA,
  output loadA,
  output no,
  output f,
  output ny,
  output loadD,
  output zy,
  output nx,
  output zx,
  output writeM,
  output AorM,
  output loadPC
);

  wire and_4_out, and_5_out, and_6_out, or_1_out, or_3_out;

  or or_1 (or_1_out, zr, ng);
  and and_1 (selA, instruction[5], instruction[15]);
  or or_2 (loadA, instruction[5], ~instruction[15]);  // OR_Gate
  and and_2 (loadD, instruction[4], instruction[15]);
  and and_3 (writeM, instruction[3], instruction[15]);
  and and_4 (and_4_out, instruction[0], or_1_out);
  and and_5 (and_5_out, instruction[1], zr);
  and and_6 (and_6_out, instruction[2], ng);
  or or_3 (or_3_out, and_4_out, and_5_out, and_6_out);
  and and_7 (loadPC, or_3_out, instruction[15]);

  assign AorM = instruction[12];
  assign f = instruction[7];
  assign no = instruction[6];
  assign nx = instruction[10];
  assign ny = instruction[8];
  assign zx = instruction[11];
  assign zy = instruction[9];

  // Other names for the same wires on the sheet: i0 = instruction[0]; i1 = instruction[1]; i2 = instruction[2];
  //   i3 = instruction[3]; i4 = instruction[4]; i5 = instruction[5]; i12 = instruction[12]; i13 = instruction[13];
  //   i14 = instruction[14]; i15 = instruction[15]
endmodule
