// Logisim project hack.circ as structural Verilog: 5 circuits, main circuit ALU
module ALU (
  input  [15:0] x,
  input  zx,
  input  nx,
  input  [15:0] y,
  input  zy,
  input  ny,
  input  f,
  input  no,
  output [15:0] out,
  output zr,
  output ng
);

  wire [15:0] adder_1_out, and_1_out, multiplexer_1_out, multiplexer_2_out, multiplexer_3_out,
       multiplexer_4_out, multiplexer_5_out, not_1_out, not_2_out, not_3_out;

  Multiplexer #(.width(16), .enable("false")) multiplexer_1 (
    .in0(x), .in1({16{1'b0}}), .out(multiplexer_1_out), .sel(zx));
  Multiplexer #(.width(16), .enable("false")) multiplexer_2 (
    .in0(y), .in1({16{1'b0}}), .out(multiplexer_2_out), .sel(zy));
  assign not_1_out = ~multiplexer_1_out;  // NOT_Gate not_1, 16 bits wide
  assign not_2_out = ~multiplexer_2_out;  // NOT_Gate not_2, 16 bits wide
  Multiplexer #(.width(16), .enable("false")) multiplexer_3 (
    .in0(multiplexer_1_out), .in1(not_1_out), .out(multiplexer_3_out), .sel(nx));
  Multiplexer #(.width(16), .enable("false")) multiplexer_4 (
    .in0(multiplexer_2_out), .in1(not_2_out), .out(multiplexer_4_out), .sel(ny));
  assign and_1_out = multiplexer_3_out & multiplexer_4_out;  // AND_Gate and_1, 16 bits wide
  Adder #(.width(16)) adder_1 (.a(multiplexer_3_out), .b(multiplexer_4_out), .out(adder_1_out));  // open: cin, cout
  Multiplexer #(.width(16), .enable("false")) multiplexer_5 (
    .in0(and_1_out), .in1(adder_1_out), .out(multiplexer_5_out), .sel(f));
  assign not_3_out = ~multiplexer_5_out;  // NOT_Gate not_3, 16 bits wide
  Multiplexer #(.width(16), .enable("false")) multiplexer_6 (
    .in0(multiplexer_5_out), .in1(not_3_out), .out({ng, out[14:0]}), .sel(no));
  nor nor_1 (zr, out[0], out[1], out[2], out[3], out[4], out[5], out[6], out[7], out[8], out[9], out[10], out[11], out[12], out[13], out[14], ng);

  assign out[15] = ng;
endmodule

module PC (
  input  reset,
  input  load,
  input  inc,
  input  clk,
  input  [15:0] in,
  output [15:0] out
);

  wire or_1_out;
  wire [15:0] adder_1_out, multiplexer_1_out;

  or or_1 (or_1_out, reset, load, inc);
  Adder #(.width(16)) adder_1 (.a(out), .b(16'h1), .out(adder_1_out), .cin(1'b0));  // open: cout
  Register #(.width(16)) register_1 (.D(multiplexer_1_out), .en(or_1_out), .Q(out), .clk(clk), .clr(1'b0));
  Multiplexer #(.select(3), .width(16), .enable("false")) multiplexer_1 (
    .in0({16{1'b0}}), .in1(adder_1_out), .in2(in), .in3(in), .in4({16{1'b0}}), .in5({16{1'b0}}),
    .in6({16{1'b0}}), .in7({16{1'b0}}), .out(multiplexer_1_out), .sel({reset, load, inc}));
endmodule

module CPU (
  input  clk,
  input  [15:0] Instruction,
  input  [15:0] inM,
  input  Reset,
  output [15:0] outM,
  output writeM,
  output [14:0] addressM,
  output [14:0] pc
);

  wire and_1_out, and_2_out, and_3_out, loadA, loadD, loadPC, ng, not_1_out, or_1_out, or_2_out, selA, zr;
  wire [15:0] D_q, multiplexer_1_out, multiplexer_2_out;
  wire [15:15] A_q, pc_1_out;

  or or_1 (or_1_out, zr, ng);
  and and_1 (and_1_out, Instruction[0], not_1_out);
  not not_1 (not_1_out, or_1_out);
  and and_2 (and_2_out, Instruction[1], zr);
  and and_3 (and_3_out, Instruction[2], ng);
  Multiplexer #(.width(16), .enable("false")) multiplexer_1 (
    .in0(Instruction), .in1(outM), .out(multiplexer_1_out), .sel(selA));
  Register #(.width(16)) A (.D(multiplexer_1_out), .en(loadA), .Q({A_q[15], addressM}), .clk(clk));  // open: clr
  or or_2 (or_2_out, and_1_out, and_2_out, and_3_out);
  Register #(.width(16)) D (.D(outM), .en(loadD), .Q(D_q), .clk(clk));  // open: clr
  Multiplexer #(.width(16), .enable("false")) multiplexer_2 (
    .in0({A_q[15], addressM}), .in1(inM), .out(multiplexer_2_out), .sel(Instruction[12]));
  and and_4 (loadPC, or_2_out, Instruction[15]);
  ALU alu_1 (
    .x(D_q), .y(multiplexer_2_out), .zx(Instruction[11]), .nx(Instruction[10]), .zy(Instruction[9]),
    .ny(Instruction[8]), .f(Instruction[7]), .no(Instruction[6]), .out(outM), .ng(ng), .zr(zr));
  PC pc_1 (.reset(Reset), .load(loadPC), .inc(1'b1), .clk(clk), .in({A_q[15], addressM}), .out({pc_1_out[15], pc}));
  and and_5 (selA, Instruction[5], Instruction[15]);
  or or_3 (loadA, Instruction[5], ~Instruction[15]);  // OR_Gate
  and and_6 (loadD, Instruction[4], Instruction[15]);
  and and_7 (writeM, Instruction[3], Instruction[15]);

  // Other names for the same wires on the sheet: i0 = Instruction[0]; i1 = Instruction[1]; i2 = Instruction[2];
  //   i3 = Instruction[3]; i4 = Instruction[4]; i5 = Instruction[5]; no = Instruction[6]; f = Instruction[7];
  //   ny = Instruction[8]; zy = Instruction[9]; nx = Instruction[10]; zx = Instruction[11]; AorM = Instruction[12];
  //   i12 = Instruction[12]; i13 = Instruction[13]; i14 = Instruction[14]; i15 = Instruction[15]
endmodule

module Computer (
);

  wire and_1_out, button_1_out, clock_1_out, cpu_1_writem;
  wire [14:0] cpu_1_addressm, cpu_1_pc;
  wire [15:0] cpu_1_outm, display_driver_1_out0, display_driver_1_out1, display_driver_1_out2,
       display_driver_1_out3, display_driver_1_out4, display_driver_1_out5, display_driver_1_out6,
       display_driver_1_out7, display_driver_1_out8, display_driver_1_out9, display_driver_1_out10,
       display_driver_1_out11, display_driver_1_out12, display_driver_1_out13, display_driver_1_out14,
       display_driver_1_out15, display_driver_1_out16, display_driver_1_out17, display_driver_1_out18,
       display_driver_1_out19, display_driver_1_out20, display_driver_1_out21, display_driver_1_out22,
       display_driver_1_out23, display_driver_1_out24, display_driver_1_out25, display_driver_1_out26,
       display_driver_1_out27, display_driver_1_out28, display_driver_1_out29, display_driver_1_out30,
       display_driver_1_out31, ram_1_data, rom_1_data;

  ROM #(.addrWidth(15), .dataWidth(16)) rom_1 (.addr(cpu_1_pc), .data(rom_1_data), .sel(1'b1));
  Clock clock_1 (.out(clock_1_out));
  Button button_1 (.out(button_1_out));
  CPU cpu_1 (
    .clk(clock_1_out), .Instruction(rom_1_data), .inM(ram_1_data), .Reset(button_1_out), .outM(cpu_1_outm),
    .writeM(cpu_1_writem), .addressM(cpu_1_addressm), .pc(cpu_1_pc));
  RAM #(.addrWidth(15), .dataWidth(16), .bus("separate")) ram_1 (
    .addr(cpu_1_addressm), .din(cpu_1_outm), .data(ram_1_data), .str(cpu_1_writem), .sel(1'b1),
    .clk(clock_1_out), .ld(1'b1), .clr(1'b0));
  DotMatrix #(.matrixcols(32), .matrixrows(16)) dotmatrix_1 (
    .col0(display_driver_1_out0), .col1(display_driver_1_out8), .col2(display_driver_1_out16),
    .col3(display_driver_1_out24), .col4(display_driver_1_out1), .col5(display_driver_1_out9),
    .col6(display_driver_1_out17), .col7(display_driver_1_out25), .col8(display_driver_1_out2),
    .col9(display_driver_1_out10), .col10(display_driver_1_out18), .col11(display_driver_1_out26),
    .col12(display_driver_1_out3), .col13(display_driver_1_out11), .col14(display_driver_1_out19),
    .col15(display_driver_1_out27), .col16(display_driver_1_out4), .col17(display_driver_1_out12),
    .col18(display_driver_1_out20), .col19(display_driver_1_out28), .col20(display_driver_1_out5),
    .col21(display_driver_1_out13), .col22(display_driver_1_out21), .col23(display_driver_1_out29),
    .col24(display_driver_1_out6), .col25(display_driver_1_out14), .col26(display_driver_1_out22),
    .col27(display_driver_1_out30), .col28(display_driver_1_out7), .col29(display_driver_1_out15),
    .col30(display_driver_1_out23), .col31(display_driver_1_out31));
  and and_1 (and_1_out, cpu_1_addressm[14], cpu_1_writem);
  Display_Driver display_driver_1 (
    .in(cpu_1_outm), .clk(clock_1_out), .load(and_1_out), .address(cpu_1_addressm[4:0]),
    .out0(display_driver_1_out0), .out8(display_driver_1_out8), .out16(display_driver_1_out16),
    .out24(display_driver_1_out24), .out1(display_driver_1_out1), .out9(display_driver_1_out9),
    .out17(display_driver_1_out17), .out25(display_driver_1_out25), .out2(display_driver_1_out2),
    .out10(display_driver_1_out10), .out18(display_driver_1_out18), .out26(display_driver_1_out26),
    .out3(display_driver_1_out3), .out11(display_driver_1_out11), .out19(display_driver_1_out19),
    .out27(display_driver_1_out27), .out4(display_driver_1_out4), .out12(display_driver_1_out12),
    .out20(display_driver_1_out20), .out28(display_driver_1_out28), .out5(display_driver_1_out5),
    .out13(display_driver_1_out13), .out21(display_driver_1_out21), .out29(display_driver_1_out29),
    .out6(display_driver_1_out6), .out14(display_driver_1_out14), .out22(display_driver_1_out22),
    .out30(display_driver_1_out30), .out7(display_driver_1_out7), .out15(display_driver_1_out15),
    .out23(display_driver_1_out23), .out31(display_driver_1_out31));

  // Notes on the sheet:
  //   contents of rom_1 (hex, n*v repeats v):
  //   5555 ec10 10 e308 5556 ec10 11 e3c8 4020 ec10 12 e308 13 ea88 4000 ec10 14 e308 13 fc10 1f e302 13
  //   ea88 11 fc10 14 fc20 e308 26 ea87 13 efc8 10 fc10 14 fc20 e308 14 fdd8 12 f1d0 e e304 12 ea87
endmodule

module Display_Driver (
  input  [15:0] in,
  input  clk,
  input  load,
  input  [4:0] address,
  output [15:0] out0,
  output [15:0] out8,
  output [15:0] out16,
  output [15:0] out24,
  output [15:0] out1,
  output [15:0] out9,
  output [15:0] out17,
  output [15:0] out25,
  output [15:0] out2,
  output [15:0] out10,
  output [15:0] out18,
  output [15:0] out26,
  output [15:0] out3,
  output [15:0] out11,
  output [15:0] out19,
  output [15:0] out27,
  output [15:0] out4,
  output [15:0] out12,
  output [15:0] out20,
  output [15:0] out28,
  output [15:0] out5,
  output [15:0] out13,
  output [15:0] out21,
  output [15:0] out29,
  output [15:0] out6,
  output [15:0] out14,
  output [15:0] out22,
  output [15:0] out30,
  output [15:0] out7,
  output [15:0] out15,
  output [15:0] out23,
  output [15:0] out31
);

  wire load0, load1, load2, load3, load4, load5, load6, load7, load8, load9, load10, load11, load12, load13,
       load14, load15, load16, load17, load18, load19, load20, load21, load22, load23, load24, load25,
       load26, load27, load28, load29, load30, load31;

  Demultiplexer #(.select(5), .enable("false")) demultiplexer_1 (
    .out0(load0), .out1(load1), .out2(load2), .out3(load3), .out4(load4), .out5(load5), .out6(load6),
    .out7(load7), .out8(load8), .out9(load9), .out10(load10), .out11(load11), .out12(load12), .out13(load13),
    .out14(load14), .out15(load15), .out16(load16), .out17(load17), .out18(load18), .out19(load19),
    .out20(load20), .out21(load21), .out22(load22), .out23(load23), .out24(load24), .out25(load25),
    .out26(load26), .out27(load27), .out28(load28), .out29(load29), .out30(load30), .out31(load31),
    .in(load), .sel(address));
  Register #(.width(16)) register_1 (.D(in), .en(load0), .Q(out0), .clk(clk), .clr(1'b0));
  Register #(.width(16)) register_2 (.D(in), .en(load1), .Q(out1), .clk(clk), .clr(1'b0));
  Register #(.width(16)) register_3 (.D(in), .en(load2), .Q(out2), .clk(clk), .clr(1'b0));
  Register #(.width(16)) register_4 (.D(in), .en(load3), .Q(out3), .clk(clk), .clr(1'b0));
  Register #(.width(16)) register_5 (.D(in), .en(load4), .Q(out4), .clk(clk), .clr(1'b0));
  Register #(.width(16)) register_6 (.D(in), .en(load5), .Q(out5), .clk(clk), .clr(1'b0));
  Register #(.width(16)) register_7 (.D(in), .en(load6), .Q(out6), .clk(clk), .clr(1'b0));
  Register #(.width(16)) register_8 (.D(in), .en(load7), .Q(out7), .clk(clk), .clr(1'b0));
  Register #(.width(16)) register_9 (.D(in), .en(load8), .Q(out8), .clk(clk), .clr(1'b0));
  Register #(.width(16)) register_10 (.D(in), .en(load9), .Q(out9), .clk(clk), .clr(1'b0));
  Register #(.width(16)) register_11 (.D(in), .en(load10), .Q(out10), .clk(clk), .clr(1'b0));
  Register #(.width(16)) register_12 (.D(in), .en(load11), .Q(out11), .clk(clk), .clr(1'b0));
  Register #(.width(16)) register_13 (.D(in), .en(load12), .Q(out12), .clk(clk), .clr(1'b0));
  Register #(.width(16)) register_14 (.D(in), .en(load13), .Q(out13), .clk(clk), .clr(1'b0));
  Register #(.width(16)) register_15 (.D(in), .en(load14), .Q(out14), .clk(clk), .clr(1'b0));
  Register #(.width(16)) register_16 (.D(in), .en(load15), .Q(out15), .clk(clk), .clr(1'b0));
  Register #(.width(16)) register_17 (.D(in), .en(load16), .Q(out16), .clk(clk), .clr(1'b0));
  Register #(.width(16)) register_18 (.D(in), .en(load17), .Q(out17), .clk(clk), .clr(1'b0));
  Register #(.width(16)) register_19 (.D(in), .en(load18), .Q(out18), .clk(clk), .clr(1'b0));
  Register #(.width(16)) register_20 (.D(in), .en(load19), .Q(out19), .clk(clk), .clr(1'b0));
  Register #(.width(16)) register_21 (.D(in), .en(load20), .Q(out20), .clk(clk), .clr(1'b0));
  Register #(.width(16)) register_22 (.D(in), .en(load21), .Q(out21), .clk(clk), .clr(1'b0));
  Register #(.width(16)) register_23 (.D(in), .en(load22), .Q(out22), .clk(clk), .clr(1'b0));
  Register #(.width(16)) register_24 (.D(in), .en(load23), .Q(out23), .clk(clk), .clr(1'b0));
  Register #(.width(16)) register_25 (.D(in), .en(load24), .Q(out24), .clk(clk), .clr(1'b0));
  Register #(.width(16)) register_26 (.D(in), .en(load25), .Q(out25), .clk(clk), .clr(1'b0));
  Register #(.width(16)) register_27 (.D(in), .en(load26), .Q(out26), .clk(clk), .clr(1'b0));
  Register #(.width(16)) register_28 (.D(in), .en(load27), .Q(out27), .clk(clk), .clr(1'b0));
  Register #(.width(16)) register_29 (.D(in), .en(load28), .Q(out28), .clk(clk), .clr(1'b0));
  Register #(.width(16)) register_30 (.D(in), .en(load29), .Q(out29), .clk(clk), .clr(1'b0));
  Register #(.width(16)) register_31 (.D(in), .en(load30), .Q(out30), .clk(clk), .clr(1'b0));
  Register #(.width(16)) register_32 (.D(in), .en(load31), .Q(out31), .clk(clk), .clr(1'b0));
endmodule
